# Fritzing sketch LDR with LCD 1602 (saved by Fritzing 0.9.3b)
breadboards: 1

parts:
  Part1 = Arduino Uno (Rev3)
  LCD1 = LCD screen  # not connected
  LCM1602_IIC1 = LCM1602 IIC [part_number="LCM1602 IIC" chip_label="LCM1602 IIC" package="DIP (Dual Inline) [THT]"]
  R1 = Photocell (LDR) [package=THT]
  R2 = Resistor [tolerance=±5% resistance=220 package=THT]

nets:
  N1: Part1.A0, R1.pin_1, R2.Pin_0
  N2: Part1.A4/SDA, LCM1602_IIC1.SDA
  N3: Part1.A5/SCL, LCM1602_IIC1.SCL
  5V: Part1.5V, LCM1602_IIC1.VCC, R1.pin_0, R2.Pin_1
  GND: Part1.GND, LCM1602_IIC1.GND
  N4: LCM1602_IIC1.LED_A, LCM1602_IIC1.LED_B

custom parts:
  LCM1602 IIC: I2C-Module to use a 1602 or 2004 LCD on with the wire.h libory Serial LCD Modul
